# Fritzing sketch 7 Segment Display (saved by Fritzing 0.9.3b)
breadboards: 1

parts:
  Part1 = Arduino Uno (Rev3)
  7_Segment1 = 7 Segment Display
  R1 = Resistor [tolerance=±5% resistance=220 package=THT]

nets:
  N1: Part1.D8, 7_Segment1.Segment_F
  N2: Part1.D9_PWM, 7_Segment1.Segment_G
  N3: Part1.D10_PWM/SS, 7_Segment1.Segment_E
  N4: Part1.D11_PWM/MOSI, 7_Segment1.Segment_D
  N5: Part1.GND, R1.Pin_1
  N6: Part1.D4, 7_Segment1.Segment_DP
  N7: Part1.D5_PWM, 7_Segment1.Segment_C
  N8: Part1.D6_PWM, 7_Segment1.Segment_B
  N9: Part1.D7, 7_Segment1.Segment_A
  N10: 7_Segment1.common_cathode, R1.Pin_0
